// Logisim project Reeti_dcmp_project_final.circ as structural Verilog: 10 circuits, main circuit main
module main (
  input  [7:0] A,
  input  [7:0] B,
  input  S1,
  input  S0,
  output out_5
);

  wire converter_1_out_5, converter_1_out_6, converter_1_out_7, converter_1_out_8, converter_1_out_9,
       converter_1_out_10, converter_1_out_11, converter_2_out_5, converter_2_out_6, converter_2_out_7,
       converter_2_out_8, converter_2_out_9, converter_2_out_10, converter_2_out_11, converter_3_out_5,
       converter_3_out_6, converter_3_out_7, converter_3_out_8, converter_3_out_9, converter_3_out_10,
       converter_3_out_11, converter_4_out_5, converter_4_out_6, converter_4_out_7, converter_4_out_8,
       converter_4_out_9, converter_4_out_10, converter_4_out_11;
  wire [7:0] subtractor_1_out_3;
  wire [15:0] addition_1_out_3, divider_1_q, multiplexer_1_out, multiplier_1_product;

  divider divider_1 (.B_divisor(B), .A_dividend(A), .Q(divider_1_q));  // open: Remainder
  multiplier multiplier_1 (.A(A), .product(multiplier_1_product), .B(B));
  subtractor subtractor_1 (.in_1(A), .in_2(B), .out_3({out_5, subtractor_1_out_3}));
  addition addition_1 (.in_1(A), .in_2(B), .out_3(addition_1_out_3));
  Multiplexer #(.select(2), .width(16)) multiplexer_1 (
    .in0(addition_1_out_3), .in1({{8{1'b0}}, subtractor_1_out_3}), .in2(multiplier_1_product),
    .in3(divider_1_q), .out(multiplexer_1_out), .sel({S0, S1}), .en(1'b1));
  converter converter_1 (
    .MSB(multiplexer_1_out[3]), .in_2(multiplexer_1_out[2]), .in_3(multiplexer_1_out[1]),
    .LSB(multiplexer_1_out[0]), .out_5(converter_1_out_5), .out_6(converter_1_out_6),
    .out_7(converter_1_out_7), .out_8(converter_1_out_8), .out_9(converter_1_out_9),
    .out_10(converter_1_out_10), .out_11(converter_1_out_11));
  converter converter_2 (
    .MSB(multiplexer_1_out[7]), .in_2(multiplexer_1_out[6]), .in_3(multiplexer_1_out[5]),
    .LSB(multiplexer_1_out[4]), .out_5(converter_2_out_5), .out_6(converter_2_out_6),
    .out_7(converter_2_out_7), .out_8(converter_2_out_8), .out_9(converter_2_out_9),
    .out_10(converter_2_out_10), .out_11(converter_2_out_11));
  converter converter_3 (
    .MSB(multiplexer_1_out[11]), .in_2(multiplexer_1_out[10]), .in_3(multiplexer_1_out[9]),
    .LSB(multiplexer_1_out[8]), .out_5(converter_3_out_5), .out_6(converter_3_out_6),
    .out_7(converter_3_out_7), .out_8(converter_3_out_8), .out_9(converter_3_out_9),
    .out_10(converter_3_out_10), .out_11(converter_3_out_11));
  converter converter_4 (
    .MSB(multiplexer_1_out[15]), .in_2(multiplexer_1_out[14]), .in_3(multiplexer_1_out[13]),
    .LSB(multiplexer_1_out[12]), .out_5(converter_4_out_5), .out_6(converter_4_out_6),
    .out_7(converter_4_out_7), .out_8(converter_4_out_8), .out_9(converter_4_out_9),
    .out_10(converter_4_out_10), .out_11(converter_4_out_11));
  _7_Segment_Display u_7_segment_display_1 (
    .g(converter_4_out_11), .f(converter_4_out_9), .a(converter_4_out_10), .b(converter_4_out_5),
    .e(converter_4_out_8), .d(converter_4_out_7), .c(converter_4_out_6));  // open: dp
  _7_Segment_Display u_7_segment_display_2 (
    .g(converter_3_out_11), .f(converter_3_out_9), .a(converter_3_out_10), .b(converter_3_out_5),
    .e(converter_3_out_8), .d(converter_3_out_7), .c(converter_3_out_6));  // open: dp
  _7_Segment_Display u_7_segment_display_3 (
    .g(converter_2_out_11), .f(converter_2_out_9), .a(converter_2_out_10), .b(converter_2_out_5),
    .e(converter_2_out_8), .d(converter_2_out_7), .c(converter_2_out_6));  // open: dp
  _7_Segment_Display u_7_segment_display_4 (
    .g(converter_1_out_11), .f(converter_1_out_9), .a(converter_1_out_10), .b(converter_1_out_5),
    .e(converter_1_out_8), .d(converter_1_out_7), .c(converter_1_out_6));  // open: dp

  // Notes on the sheet:
  //   Select   lines
  //   Addition - S1=0,S0=0
  //   Subtraction - S1=1,S0=0
  //   Multiplication - S1=0,S0=1
  //   Division - S1=1,S0=1
endmodule

module fulladder_alu (
  input  A,
  input  B,
  input  Cin,
  output sum,
  output carry
);

  wire not_1_out;

  not not_1 (not_1_out, A);
  Multiplexer #(.select(2)) multiplexer_1 (
    .in0(A), .in1(not_1_out), .in2(not_1_out), .in3(A), .out(sum), .sel({Cin, B}), .en(1'b1));
  Multiplexer #(.select(2)) multiplexer_2 (
    .in0(1'b0), .in1(A), .in2(A), .in3(1'b1), .out(carry), .sel({Cin, B}), .en(1'b1));
endmodule

module additionoperator (
  input  [7:0] in_1,
  input  [7:0] in_2,
  output [7:0] out_3,
  output carry
);

  wire fulladder_alu_1_carry, fulladder_alu_2_carry, fulladder_alu_3_carry, fulladder_alu_4_carry,
       fulladder_alu_5_carry, fulladder_alu_6_carry, fulladder_alu_7_carry;

  fulladder_alu fulladder_alu_1 (.A(1'b0), .B(in_1[0]), .Cin(in_2[0]), .sum(out_3[0]), .carry(fulladder_alu_1_carry));
  fulladder_alu fulladder_alu_2 (
    .A(fulladder_alu_1_carry), .B(in_1[1]), .Cin(in_2[1]), .sum(out_3[1]), .carry(fulladder_alu_2_carry));
  fulladder_alu fulladder_alu_3 (
    .A(fulladder_alu_2_carry), .B(in_1[2]), .Cin(in_2[2]), .sum(out_3[2]), .carry(fulladder_alu_3_carry));
  fulladder_alu fulladder_alu_4 (
    .A(fulladder_alu_3_carry), .B(in_1[3]), .Cin(in_2[3]), .sum(out_3[3]), .carry(fulladder_alu_4_carry));
  fulladder_alu fulladder_alu_5 (
    .A(fulladder_alu_4_carry), .B(in_1[4]), .Cin(in_2[4]), .sum(out_3[4]), .carry(fulladder_alu_5_carry));
  fulladder_alu fulladder_alu_6 (
    .A(fulladder_alu_5_carry), .B(in_1[5]), .Cin(in_2[5]), .sum(out_3[5]), .carry(fulladder_alu_6_carry));
  fulladder_alu fulladder_alu_7 (
    .A(fulladder_alu_6_carry), .B(in_1[6]), .Cin(in_2[6]), .sum(out_3[6]), .carry(fulladder_alu_7_carry));
  fulladder_alu fulladder_alu_8 (.A(fulladder_alu_7_carry), .B(in_1[7]), .Cin(in_2[7]), .sum(out_3[7]), .carry(carry));

  // Notes on the sheet:
  //   A
  //   B
  //   LSB
  //   C0
  //   C1
  //   C2
  //   C3
  //   C4
  //   C5
  //   C6
  //   C7
  //   MSB
  //   sum
endmodule

module subtractionoperator (
  input  [7:0] in_1,
  input  [7:0] in_2,
  output [7:0] out_3,
  output borrow
);

  wire fulladder_alu_1_carry, fulladder_alu_2_carry, fulladder_alu_3_carry, fulladder_alu_4_carry,
       fulladder_alu_5_carry, fulladder_alu_6_carry, fulladder_alu_7_carry, xor_1_out, xor_2_out, xor_3_out,
       xor_4_out, xor_5_out, xor_6_out, xor_7_out, xor_8_out;

  xor xor_1 (xor_1_out, 1'b1, in_2[0]);
  xor xor_2 (xor_2_out, 1'b1, in_2[1]);
  xor xor_3 (xor_3_out, 1'b1, in_2[2]);
  xor xor_4 (xor_4_out, 1'b1, in_2[3]);
  xor xor_5 (xor_5_out, 1'b1, in_2[4]);
  xor xor_6 (xor_6_out, 1'b1, in_2[5]);
  xor xor_7 (xor_7_out, 1'b1, in_2[6]);
  xor xor_8 (xor_8_out, 1'b1, in_2[7]);
  fulladder_alu fulladder_alu_1 (.A(1'b1), .B(in_1[0]), .Cin(xor_1_out), .sum(out_3[0]), .carry(fulladder_alu_1_carry));
  fulladder_alu fulladder_alu_2 (
    .A(fulladder_alu_1_carry), .B(in_1[1]), .Cin(xor_2_out), .sum(out_3[1]), .carry(fulladder_alu_2_carry));
  fulladder_alu fulladder_alu_3 (
    .A(fulladder_alu_2_carry), .B(in_1[2]), .Cin(xor_3_out), .sum(out_3[2]), .carry(fulladder_alu_3_carry));
  fulladder_alu fulladder_alu_4 (
    .A(fulladder_alu_3_carry), .B(in_1[3]), .Cin(xor_4_out), .sum(out_3[3]), .carry(fulladder_alu_4_carry));
  fulladder_alu fulladder_alu_5 (
    .A(fulladder_alu_4_carry), .B(in_1[4]), .Cin(xor_5_out), .sum(out_3[4]), .carry(fulladder_alu_5_carry));
  fulladder_alu fulladder_alu_6 (
    .A(fulladder_alu_5_carry), .B(in_1[5]), .Cin(xor_6_out), .sum(out_3[5]), .carry(fulladder_alu_6_carry));
  fulladder_alu fulladder_alu_7 (
    .A(fulladder_alu_6_carry), .B(in_1[6]), .Cin(xor_7_out), .sum(out_3[6]), .carry(fulladder_alu_7_carry));
  fulladder_alu fulladder_alu_8 (
    .A(fulladder_alu_7_carry), .B(in_1[7]), .Cin(xor_8_out), .sum(out_3[7]), .carry(borrow));

  // Notes on the sheet:
  //   A
  //   B
  //   K
  //   difference
endmodule

module multiplier (
  input  [7:0] A,
  input  [7:0] B,
  output [15:0] product
);

  wire [6:0] and_2_out;
  wire [7:0] and_9_out, and_17_out, and_25_out, and_33_out, and_41_out, and_49_out, and_57_out;
  wire [7:1] additionoperator_1_out_3, additionoperator_2_out_3, additionoperator_3_out_3,
       additionoperator_4_out_3, additionoperator_5_out_3, additionoperator_6_out_3;
  wire [7:7] additionoperator_1_carry, additionoperator_2_carry, additionoperator_3_carry,
       additionoperator_4_carry, additionoperator_5_carry, additionoperator_6_carry;

  and and_1 (product[0], A[0], B[0]);
  and and_2 (and_2_out[0], A[1], B[0]);
  and and_3 (and_2_out[1], A[2], B[0]);
  and and_4 (and_2_out[2], A[3], B[0]);
  and and_5 (and_2_out[3], A[4], B[0]);
  and and_6 (and_2_out[4], A[5], B[0]);
  and and_7 (and_2_out[5], A[6], B[0]);
  and and_8 (and_2_out[6], A[7], B[0]);
  and and_9 (and_9_out[0], A[0], B[1]);
  and and_10 (and_9_out[1], A[1], B[1]);
  and and_11 (and_9_out[2], A[2], B[1]);
  and and_12 (and_9_out[3], A[3], B[1]);
  and and_13 (and_9_out[4], A[4], B[1]);
  and and_14 (and_9_out[5], A[5], B[1]);
  and and_15 (and_9_out[6], A[6], B[1]);
  and and_16 (and_9_out[7], A[7], B[1]);
  additionoperator additionoperator_1 (
    .in_1({1'b0, and_2_out}), .in_2(and_9_out), .out_3({additionoperator_1_out_3, product[1]}),
    .carry(additionoperator_1_carry[7]));
  and and_17 (and_17_out[0], A[0], B[2]);
  and and_18 (and_17_out[1], A[1], B[2]);
  and and_19 (and_17_out[2], A[2], B[2]);
  and and_20 (and_17_out[3], A[3], B[2]);
  and and_21 (and_17_out[4], A[4], B[2]);
  and and_22 (and_17_out[5], A[5], B[2]);
  and and_23 (and_17_out[6], A[6], B[2]);
  and and_24 (and_17_out[7], A[7], B[2]);
  additionoperator additionoperator_2 (
    .in_1({additionoperator_1_carry[7], additionoperator_1_out_3}), .in_2(and_17_out),
    .out_3({additionoperator_2_out_3, product[2]}), .carry(additionoperator_2_carry[7]));
  and and_25 (and_25_out[0], A[0], B[3]);
  and and_26 (and_25_out[1], A[1], B[3]);
  and and_27 (and_25_out[2], A[2], B[3]);
  and and_28 (and_25_out[3], A[3], B[3]);
  and and_29 (and_25_out[4], A[4], B[3]);
  and and_30 (and_25_out[5], A[5], B[3]);
  and and_31 (and_25_out[6], A[6], B[3]);
  and and_32 (and_25_out[7], A[7], B[3]);
  additionoperator additionoperator_3 (
    .in_1({additionoperator_2_carry[7], additionoperator_2_out_3}), .in_2(and_25_out),
    .out_3({additionoperator_3_out_3, product[3]}), .carry(additionoperator_3_carry[7]));
  and and_33 (and_33_out[0], A[0], B[4]);
  and and_34 (and_33_out[1], A[1], B[4]);
  and and_35 (and_33_out[2], A[2], B[4]);
  and and_36 (and_33_out[3], A[3], B[4]);
  and and_37 (and_33_out[4], A[4], B[4]);
  and and_38 (and_33_out[5], A[5], B[4]);
  and and_39 (and_33_out[6], A[6], B[4]);
  and and_40 (and_33_out[7], A[7], B[4]);
  additionoperator additionoperator_4 (
    .in_1({additionoperator_3_carry[7], additionoperator_3_out_3}), .in_2(and_33_out),
    .out_3({additionoperator_4_out_3, product[4]}), .carry(additionoperator_4_carry[7]));
  and and_41 (and_41_out[0], A[0], B[5]);
  and and_42 (and_41_out[1], A[1], B[5]);
  and and_43 (and_41_out[2], A[2], B[5]);
  and and_44 (and_41_out[3], A[3], B[5]);
  and and_45 (and_41_out[4], A[4], B[5]);
  and and_46 (and_41_out[5], A[5], B[5]);
  and and_47 (and_41_out[6], A[6], B[5]);
  and and_48 (and_41_out[7], A[7], B[5]);
  additionoperator additionoperator_5 (
    .in_1({additionoperator_4_carry[7], additionoperator_4_out_3}), .in_2(and_41_out),
    .out_3({additionoperator_5_out_3, product[5]}), .carry(additionoperator_5_carry[7]));
  and and_49 (and_49_out[0], A[0], B[6]);
  and and_50 (and_49_out[1], A[1], B[6]);
  and and_51 (and_49_out[2], A[2], B[6]);
  and and_52 (and_49_out[3], A[3], B[6]);
  and and_53 (and_49_out[4], A[4], B[6]);
  and and_54 (and_49_out[5], A[5], B[6]);
  and and_55 (and_49_out[6], A[6], B[6]);
  and and_56 (and_49_out[7], A[7], B[6]);
  additionoperator additionoperator_6 (
    .in_1({additionoperator_5_carry[7], additionoperator_5_out_3}), .in_2(and_49_out),
    .out_3({additionoperator_6_out_3, product[6]}), .carry(additionoperator_6_carry[7]));
  and and_57 (and_57_out[0], A[0], B[7]);
  and and_58 (and_57_out[1], A[1], B[7]);
  and and_59 (and_57_out[2], A[2], B[7]);
  and and_60 (and_57_out[3], A[3], B[7]);
  and and_61 (and_57_out[4], A[4], B[7]);
  and and_62 (and_57_out[5], A[5], B[7]);
  and and_63 (and_57_out[6], A[6], B[7]);
  and and_64 (and_57_out[7], A[7], B[7]);
  additionoperator additionoperator_7 (
    .in_1({additionoperator_6_carry[7], additionoperator_6_out_3}), .in_2(and_57_out), .out_3(product[14:7]),
    .carry(product[15]));

  // Notes on the sheet:
  //   product
endmodule

module divider (
  input  [7:0] B_divisor,
  input  [7:0] A_dividend,
  output [15:0] Q,
  output [15:0] Remainder
);

  wire fulladder_alu_1_carry, fulladder_alu_1_sum, fulladder_alu_2_carry, fulladder_alu_2_sum,
       fulladder_alu_3_carry, fulladder_alu_3_sum, fulladder_alu_4_carry, fulladder_alu_4_sum,
       fulladder_alu_5_carry, fulladder_alu_5_sum, fulladder_alu_6_carry, fulladder_alu_6_sum,
       fulladder_alu_7_carry, fulladder_alu_7_sum, fulladder_alu_8_carry, fulladder_alu_8_sum,
       fulladder_alu_9_carry, fulladder_alu_9_sum, fulladder_alu_10_carry, fulladder_alu_10_sum,
       fulladder_alu_11_carry, fulladder_alu_11_sum, fulladder_alu_12_carry, fulladder_alu_12_sum,
       fulladder_alu_13_carry, fulladder_alu_13_sum, fulladder_alu_14_carry, fulladder_alu_14_sum,
       fulladder_alu_15_carry, fulladder_alu_15_sum, fulladder_alu_16_carry, fulladder_alu_16_sum,
       fulladder_alu_17_carry, fulladder_alu_17_sum, fulladder_alu_18_carry, fulladder_alu_18_sum,
       fulladder_alu_19_carry, fulladder_alu_19_sum, fulladder_alu_20_carry, fulladder_alu_20_sum,
       fulladder_alu_21_carry, fulladder_alu_21_sum, fulladder_alu_22_carry, fulladder_alu_22_sum,
       fulladder_alu_23_carry, fulladder_alu_23_sum, fulladder_alu_24_carry, fulladder_alu_24_sum,
       fulladder_alu_25_carry, fulladder_alu_25_sum, fulladder_alu_26_carry, fulladder_alu_26_sum,
       fulladder_alu_27_carry, fulladder_alu_27_sum, fulladder_alu_28_carry, fulladder_alu_28_sum,
       fulladder_alu_29_carry, fulladder_alu_29_sum, fulladder_alu_30_carry, fulladder_alu_30_sum,
       fulladder_alu_31_sum, fulladder_alu_32_carry, fulladder_alu_32_sum, fulladder_alu_33_carry,
       fulladder_alu_33_sum, fulladder_alu_34_carry, fulladder_alu_34_sum, fulladder_alu_35_carry,
       fulladder_alu_35_sum, fulladder_alu_36_carry, fulladder_alu_36_sum, fulladder_alu_37_carry,
       fulladder_alu_37_sum, fulladder_alu_38_carry, fulladder_alu_38_sum, fulladder_alu_39_carry,
       fulladder_alu_39_sum, fulladder_alu_40_carry, fulladder_alu_40_sum, fulladder_alu_41_carry,
       fulladder_alu_41_sum, fulladder_alu_42_carry, fulladder_alu_42_sum, fulladder_alu_43_sum,
       fulladder_alu_44_carry, fulladder_alu_44_sum, fulladder_alu_45_carry, fulladder_alu_45_sum,
       fulladder_alu_46_carry, fulladder_alu_46_sum, fulladder_alu_47_carry, fulladder_alu_47_sum,
       fulladder_alu_48_carry, fulladder_alu_48_sum, fulladder_alu_49_sum, fulladder_alu_50_carry,
       fulladder_alu_50_sum, fulladder_alu_51_carry, fulladder_alu_51_sum, fulladder_alu_52_carry,
       fulladder_alu_52_sum, fulladder_alu_53_carry, fulladder_alu_53_sum, fulladder_alu_54_sum,
       fulladder_alu_55_carry, fulladder_alu_55_sum, fulladder_alu_56_carry, fulladder_alu_56_sum,
       fulladder_alu_57_carry, fulladder_alu_57_sum, fulladder_alu_58_sum, fulladder_alu_59_carry,
       fulladder_alu_59_sum, fulladder_alu_60_carry, fulladder_alu_60_sum, fulladder_alu_61_sum,
       fulladder_alu_62_carry, fulladder_alu_62_sum, fulladder_alu_63_sum, fulladder_alu_64_sum,
       multiplexer_2_out, multiplexer_4_out, multiplexer_6_out, multiplexer_7_out, multiplexer_8_out,
       multiplexer_9_out, multiplexer_11_out, multiplexer_12_out, multiplexer_13_out, multiplexer_14_out,
       multiplexer_16_out, multiplexer_17_out, multiplexer_18_out, multiplexer_19_out, multiplexer_20_out,
       multiplexer_22_out, multiplexer_23_out, multiplexer_24_out, multiplexer_25_out, multiplexer_26_out,
       multiplexer_27_out, multiplexer_29_out, multiplexer_30_out, multiplexer_32_out, multiplexer_33_out,
       multiplexer_34_out, multiplexer_35_out, multiplexer_36_out, multiplexer_37_out, multiplexer_38_out,
       multiplexer_39_out, multiplexer_40_out, multiplexer_41_out, multiplexer_42_out, multiplexer_44_out,
       multiplexer_45_out, multiplexer_46_out, multiplexer_47_out, multiplexer_48_out, multiplexer_50_out,
       multiplexer_51_out, multiplexer_52_out, multiplexer_53_out, multiplexer_55_out, multiplexer_56_out,
       multiplexer_57_out, multiplexer_59_out, multiplexer_60_out, multiplexer_62_out, not_1_out, not_2_out,
       not_3_out, not_4_out, not_5_out, not_6_out, not_7_out, not_8_out, not_9_out;

  fulladder_alu fulladder_alu_1 (
    .A(A_dividend[0]), .B(not_2_out), .Cin(1'b1), .sum(fulladder_alu_1_sum), .carry(fulladder_alu_1_carry));
  Multiplexer multiplexer_1 (.in0(A_dividend[0]), .in1(fulladder_alu_1_sum), .out(Remainder[0]), .sel(Q[0]), .en(1'b1));
  fulladder_alu fulladder_alu_2 (
    .A(A_dividend[1]), .B(not_2_out), .Cin(1'b1), .sum(fulladder_alu_2_sum), .carry(fulladder_alu_2_carry));
  Multiplexer multiplexer_2 (
    .in0(A_dividend[1]), .in1(fulladder_alu_2_sum), .out(multiplexer_2_out), .sel(Q[1]), .en(1'b1));
  fulladder_alu fulladder_alu_3 (
    .A(multiplexer_2_out), .B(not_3_out), .Cin(fulladder_alu_1_carry), .sum(fulladder_alu_3_sum),
    .carry(fulladder_alu_3_carry));
  Multiplexer multiplexer_3 (
    .in0(multiplexer_2_out), .in1(fulladder_alu_3_sum), .out(Remainder[1]), .sel(Q[0]), .en(1'b1));
  fulladder_alu fulladder_alu_4 (
    .A(multiplexer_6_out), .B(not_3_out), .Cin(fulladder_alu_2_carry), .sum(fulladder_alu_4_sum),
    .carry(fulladder_alu_4_carry));
  Multiplexer multiplexer_4 (
    .in0(multiplexer_6_out), .in1(fulladder_alu_4_sum), .out(multiplexer_4_out), .sel(Q[1]), .en(1'b1));
  fulladder_alu fulladder_alu_5 (
    .A(multiplexer_4_out), .B(not_4_out), .Cin(fulladder_alu_3_carry), .sum(fulladder_alu_5_sum),
    .carry(fulladder_alu_5_carry));
  Multiplexer multiplexer_5 (
    .in0(multiplexer_4_out), .in1(fulladder_alu_5_sum), .out(Remainder[2]), .sel(Q[0]), .en(1'b1));
  fulladder_alu fulladder_alu_6 (
    .A(A_dividend[2]), .B(not_2_out), .Cin(1'b1), .sum(fulladder_alu_6_sum), .carry(fulladder_alu_6_carry));
  Multiplexer multiplexer_6 (
    .in0(A_dividend[2]), .in1(fulladder_alu_6_sum), .out(multiplexer_6_out), .sel(Q[2]), .en(1'b1));
  fulladder_alu fulladder_alu_7 (
    .A(A_dividend[3]), .B(not_2_out), .Cin(1'b1), .sum(fulladder_alu_7_sum), .carry(fulladder_alu_7_carry));
  Multiplexer multiplexer_7 (
    .in0(A_dividend[3]), .in1(fulladder_alu_7_sum), .out(multiplexer_7_out), .sel(Q[3]), .en(1'b1));
  fulladder_alu fulladder_alu_8 (
    .A(multiplexer_7_out), .B(not_3_out), .Cin(fulladder_alu_6_carry), .sum(fulladder_alu_8_sum),
    .carry(fulladder_alu_8_carry));
  Multiplexer multiplexer_8 (
    .in0(multiplexer_7_out), .in1(fulladder_alu_8_sum), .out(multiplexer_8_out), .sel(Q[2]), .en(1'b1));
  fulladder_alu fulladder_alu_9 (
    .A(multiplexer_8_out), .B(not_4_out), .Cin(fulladder_alu_4_carry), .sum(fulladder_alu_9_sum),
    .carry(fulladder_alu_9_carry));
  Multiplexer multiplexer_9 (
    .in0(multiplexer_8_out), .in1(fulladder_alu_9_sum), .out(multiplexer_9_out), .sel(Q[1]), .en(1'b1));
  fulladder_alu fulladder_alu_10 (
    .A(multiplexer_9_out), .B(not_5_out), .Cin(fulladder_alu_5_carry), .sum(fulladder_alu_10_sum),
    .carry(fulladder_alu_10_carry));
  Multiplexer multiplexer_10 (
    .in0(multiplexer_9_out), .in1(fulladder_alu_10_sum), .out(Remainder[3]), .sel(Q[0]), .en(1'b1));
  fulladder_alu fulladder_alu_11 (
    .A(A_dividend[4]), .B(not_2_out), .Cin(1'b1), .sum(fulladder_alu_11_sum), .carry(fulladder_alu_11_carry));
  Multiplexer multiplexer_11 (
    .in0(A_dividend[4]), .in1(fulladder_alu_11_sum), .out(multiplexer_11_out), .sel(Q[4]), .en(1'b1));
  fulladder_alu fulladder_alu_12 (
    .A(multiplexer_11_out), .B(not_3_out), .Cin(fulladder_alu_7_carry), .sum(fulladder_alu_12_sum),
    .carry(fulladder_alu_12_carry));
  Multiplexer multiplexer_12 (
    .in0(multiplexer_11_out), .in1(fulladder_alu_12_sum), .out(multiplexer_12_out), .sel(Q[3]), .en(1'b1));
  fulladder_alu fulladder_alu_13 (
    .A(multiplexer_12_out), .B(not_4_out), .Cin(fulladder_alu_8_carry), .sum(fulladder_alu_13_sum),
    .carry(fulladder_alu_13_carry));
  Multiplexer multiplexer_13 (
    .in0(multiplexer_12_out), .in1(fulladder_alu_13_sum), .out(multiplexer_13_out), .sel(Q[2]), .en(1'b1));
  fulladder_alu fulladder_alu_14 (
    .A(multiplexer_13_out), .B(not_5_out), .Cin(fulladder_alu_9_carry), .sum(fulladder_alu_14_sum),
    .carry(fulladder_alu_14_carry));
  Multiplexer multiplexer_14 (
    .in0(multiplexer_13_out), .in1(fulladder_alu_14_sum), .out(multiplexer_14_out), .sel(Q[1]), .en(1'b1));
  fulladder_alu fulladder_alu_15 (
    .A(multiplexer_14_out), .B(not_6_out), .Cin(fulladder_alu_10_carry), .sum(fulladder_alu_15_sum),
    .carry(fulladder_alu_15_carry));
  Multiplexer multiplexer_15 (
    .in0(multiplexer_14_out), .in1(fulladder_alu_15_sum), .out(Remainder[4]), .sel(Q[0]), .en(1'b1));
  fulladder_alu fulladder_alu_16 (
    .A(A_dividend[5]), .B(not_2_out), .Cin(1'b1), .sum(fulladder_alu_16_sum), .carry(fulladder_alu_16_carry));
  Multiplexer multiplexer_16 (
    .in0(A_dividend[5]), .in1(fulladder_alu_16_sum), .out(multiplexer_16_out), .sel(Q[5]), .en(1'b1));
  fulladder_alu fulladder_alu_17 (
    .A(multiplexer_16_out), .B(not_3_out), .Cin(fulladder_alu_11_carry), .sum(fulladder_alu_17_sum),
    .carry(fulladder_alu_17_carry));
  Multiplexer multiplexer_17 (
    .in0(multiplexer_16_out), .in1(fulladder_alu_17_sum), .out(multiplexer_17_out), .sel(Q[4]), .en(1'b1));
  fulladder_alu fulladder_alu_18 (
    .A(multiplexer_17_out), .B(not_4_out), .Cin(fulladder_alu_12_carry), .sum(fulladder_alu_18_sum),
    .carry(fulladder_alu_18_carry));
  Multiplexer multiplexer_18 (
    .in0(multiplexer_17_out), .in1(fulladder_alu_18_sum), .out(multiplexer_18_out), .sel(Q[3]), .en(1'b1));
  fulladder_alu fulladder_alu_19 (
    .A(multiplexer_18_out), .B(not_5_out), .Cin(fulladder_alu_13_carry), .sum(fulladder_alu_19_sum),
    .carry(fulladder_alu_19_carry));
  Multiplexer multiplexer_19 (
    .in0(multiplexer_18_out), .in1(fulladder_alu_19_sum), .out(multiplexer_19_out), .sel(Q[2]), .en(1'b1));
  fulladder_alu fulladder_alu_20 (
    .A(multiplexer_19_out), .B(not_6_out), .Cin(fulladder_alu_14_carry), .sum(fulladder_alu_20_sum),
    .carry(fulladder_alu_20_carry));
  Multiplexer multiplexer_20 (
    .in0(multiplexer_19_out), .in1(fulladder_alu_20_sum), .out(multiplexer_20_out), .sel(Q[1]), .en(1'b1));
  fulladder_alu fulladder_alu_21 (
    .A(multiplexer_20_out), .B(not_7_out), .Cin(fulladder_alu_15_carry), .sum(fulladder_alu_21_sum),
    .carry(fulladder_alu_21_carry));
  Multiplexer multiplexer_21 (
    .in0(multiplexer_20_out), .in1(fulladder_alu_21_sum), .out(Remainder[5]), .sel(Q[0]), .en(1'b1));
  fulladder_alu fulladder_alu_22 (
    .A(not_2_out), .B(A_dividend[6]), .Cin(1'b1), .sum(fulladder_alu_22_sum), .carry(fulladder_alu_22_carry));
  Multiplexer multiplexer_22 (
    .in0(A_dividend[6]), .in1(fulladder_alu_22_sum), .out(multiplexer_22_out), .sel(Q[6]), .en(1'b1));
  fulladder_alu fulladder_alu_23 (
    .A(multiplexer_22_out), .B(not_3_out), .Cin(fulladder_alu_16_carry), .sum(fulladder_alu_23_sum),
    .carry(fulladder_alu_23_carry));
  Multiplexer multiplexer_23 (
    .in0(multiplexer_22_out), .in1(fulladder_alu_23_sum), .out(multiplexer_23_out), .sel(Q[5]), .en(1'b1));
  fulladder_alu fulladder_alu_24 (
    .A(multiplexer_23_out), .B(not_4_out), .Cin(fulladder_alu_17_carry), .sum(fulladder_alu_24_sum),
    .carry(fulladder_alu_24_carry));
  Multiplexer multiplexer_24 (
    .in0(multiplexer_23_out), .in1(fulladder_alu_24_sum), .out(multiplexer_24_out), .sel(Q[4]), .en(1'b1));
  fulladder_alu fulladder_alu_25 (
    .A(multiplexer_24_out), .B(not_5_out), .Cin(fulladder_alu_18_carry), .sum(fulladder_alu_25_sum),
    .carry(fulladder_alu_25_carry));
  Multiplexer multiplexer_25 (
    .in0(multiplexer_24_out), .in1(fulladder_alu_25_sum), .out(multiplexer_25_out), .sel(Q[3]), .en(1'b1));
  fulladder_alu fulladder_alu_26 (
    .A(multiplexer_25_out), .B(not_6_out), .Cin(fulladder_alu_19_carry), .sum(fulladder_alu_26_sum),
    .carry(fulladder_alu_26_carry));
  Multiplexer multiplexer_26 (
    .in0(multiplexer_25_out), .in1(fulladder_alu_26_sum), .out(multiplexer_26_out), .sel(Q[2]), .en(1'b1));
  fulladder_alu fulladder_alu_27 (
    .A(multiplexer_26_out), .B(not_7_out), .Cin(fulladder_alu_20_carry), .sum(fulladder_alu_27_sum),
    .carry(fulladder_alu_27_carry));
  Multiplexer multiplexer_27 (
    .in0(multiplexer_26_out), .in1(fulladder_alu_27_sum), .out(multiplexer_27_out), .sel(Q[1]), .en(1'b1));
  fulladder_alu fulladder_alu_28 (
    .A(multiplexer_27_out), .B(not_8_out), .Cin(fulladder_alu_21_carry), .sum(fulladder_alu_28_sum),
    .carry(fulladder_alu_28_carry));
  Multiplexer multiplexer_28 (
    .in0(multiplexer_27_out), .in1(fulladder_alu_28_sum), .out(Remainder[6]), .sel(Q[0]), .en(1'b1));
  not not_1 (not_1_out, 1'b1);
  not not_2 (not_2_out, B_divisor[0]);
  fulladder_alu fulladder_alu_29 (
    .A(multiplexer_35_out), .B(not_6_out), .Cin(fulladder_alu_25_carry), .sum(fulladder_alu_29_sum),
    .carry(fulladder_alu_29_carry));
  Multiplexer multiplexer_29 (
    .in0(multiplexer_35_out), .in1(fulladder_alu_29_sum), .out(multiplexer_29_out), .sel(Q[3]), .en(1'b1));
  fulladder_alu fulladder_alu_30 (
    .A(multiplexer_36_out), .B(not_8_out), .Cin(fulladder_alu_27_carry), .sum(fulladder_alu_30_sum),
    .carry(fulladder_alu_30_carry));
  Multiplexer multiplexer_30 (
    .in0(multiplexer_36_out), .in1(fulladder_alu_30_sum), .out(multiplexer_30_out), .sel(Q[1]), .en(1'b1));
  fulladder_alu fulladder_alu_31 (
    .A(multiplexer_30_out), .B(not_9_out), .Cin(fulladder_alu_28_carry), .sum(fulladder_alu_31_sum),
    .carry(Q[0]));
  Multiplexer multiplexer_31 (
    .in0(multiplexer_30_out), .in1(fulladder_alu_31_sum), .out(Remainder[7]), .sel(Q[0]), .en(1'b1));
  fulladder_alu fulladder_alu_32 (
    .A(not_2_out), .B(A_dividend[7]), .Cin(1'b1), .sum(fulladder_alu_32_sum), .carry(fulladder_alu_32_carry));
  Multiplexer multiplexer_32 (
    .in0(A_dividend[7]), .in1(fulladder_alu_32_sum), .out(multiplexer_32_out), .sel(Q[7]), .en(1'b1));
  fulladder_alu fulladder_alu_33 (
    .A(not_3_out), .B(multiplexer_32_out), .Cin(fulladder_alu_22_carry), .sum(fulladder_alu_33_sum),
    .carry(fulladder_alu_33_carry));
  Multiplexer multiplexer_33 (
    .in0(multiplexer_32_out), .in1(fulladder_alu_33_sum), .out(multiplexer_33_out), .sel(Q[6]), .en(1'b1));
  fulladder_alu fulladder_alu_34 (
    .A(multiplexer_33_out), .B(not_4_out), .Cin(fulladder_alu_23_carry), .sum(fulladder_alu_34_sum),
    .carry(fulladder_alu_34_carry));
  Multiplexer multiplexer_34 (
    .in0(multiplexer_33_out), .in1(fulladder_alu_34_sum), .out(multiplexer_34_out), .sel(Q[5]), .en(1'b1));
  fulladder_alu fulladder_alu_35 (
    .A(multiplexer_34_out), .B(not_5_out), .Cin(fulladder_alu_24_carry), .sum(fulladder_alu_35_sum),
    .carry(fulladder_alu_35_carry));
  Multiplexer multiplexer_35 (
    .in0(multiplexer_34_out), .in1(fulladder_alu_35_sum), .out(multiplexer_35_out), .sel(Q[4]), .en(1'b1));
  fulladder_alu fulladder_alu_36 (
    .A(multiplexer_29_out), .B(not_7_out), .Cin(fulladder_alu_26_carry), .sum(fulladder_alu_36_sum),
    .carry(fulladder_alu_36_carry));
  Multiplexer multiplexer_36 (
    .in0(multiplexer_29_out), .in1(fulladder_alu_36_sum), .out(multiplexer_36_out), .sel(Q[2]), .en(1'b1));
  not not_3 (not_3_out, B_divisor[1]);
  fulladder_alu fulladder_alu_37 (
    .A(not_3_out), .B(not_1_out), .Cin(fulladder_alu_32_carry), .sum(fulladder_alu_37_sum),
    .carry(fulladder_alu_37_carry));
  Multiplexer multiplexer_37 (
    .in0(not_1_out), .in1(fulladder_alu_37_sum), .out(multiplexer_37_out), .sel(Q[7]), .en(1'b1));
  fulladder_alu fulladder_alu_38 (
    .A(not_4_out), .B(multiplexer_37_out), .Cin(fulladder_alu_33_carry), .sum(fulladder_alu_38_sum),
    .carry(fulladder_alu_38_carry));
  Multiplexer multiplexer_38 (
    .in0(multiplexer_37_out), .in1(fulladder_alu_38_sum), .out(multiplexer_38_out), .sel(Q[6]), .en(1'b1));
  fulladder_alu fulladder_alu_39 (
    .A(multiplexer_38_out), .B(not_5_out), .Cin(fulladder_alu_34_carry), .sum(fulladder_alu_39_sum),
    .carry(fulladder_alu_39_carry));
  Multiplexer multiplexer_39 (
    .in0(multiplexer_38_out), .in1(fulladder_alu_39_sum), .out(multiplexer_39_out), .sel(Q[5]), .en(1'b1));
  fulladder_alu fulladder_alu_40 (
    .A(multiplexer_39_out), .B(not_6_out), .Cin(fulladder_alu_35_carry), .sum(fulladder_alu_40_sum),
    .carry(fulladder_alu_40_carry));
  Multiplexer multiplexer_40 (
    .in0(multiplexer_39_out), .in1(fulladder_alu_40_sum), .out(multiplexer_40_out), .sel(Q[4]), .en(1'b1));
  fulladder_alu fulladder_alu_41 (
    .A(multiplexer_40_out), .B(not_7_out), .Cin(fulladder_alu_29_carry), .sum(fulladder_alu_41_sum),
    .carry(fulladder_alu_41_carry));
  Multiplexer multiplexer_41 (
    .in0(multiplexer_40_out), .in1(fulladder_alu_41_sum), .out(multiplexer_41_out), .sel(Q[3]), .en(1'b1));
  fulladder_alu fulladder_alu_42 (
    .A(multiplexer_41_out), .B(not_8_out), .Cin(fulladder_alu_36_carry), .sum(fulladder_alu_42_sum),
    .carry(fulladder_alu_42_carry));
  Multiplexer multiplexer_42 (
    .in0(multiplexer_41_out), .in1(fulladder_alu_42_sum), .out(multiplexer_42_out), .sel(Q[2]), .en(1'b1));
  fulladder_alu fulladder_alu_43 (
    .A(multiplexer_42_out), .B(not_9_out), .Cin(fulladder_alu_30_carry), .sum(fulladder_alu_43_sum),
    .carry(Q[1]));
  Multiplexer multiplexer_43 (
    .in0(multiplexer_42_out), .in1(fulladder_alu_43_sum), .sel(Q[1]), .en(1'b1));  // open: out
  not not_4 (not_4_out, B_divisor[2]);
  fulladder_alu fulladder_alu_44 (
    .A(not_4_out), .B(not_1_out), .Cin(fulladder_alu_37_carry), .sum(fulladder_alu_44_sum),
    .carry(fulladder_alu_44_carry));
  Multiplexer multiplexer_44 (
    .in0(not_1_out), .in1(fulladder_alu_44_sum), .out(multiplexer_44_out), .sel(Q[7]), .en(1'b1));
  fulladder_alu fulladder_alu_45 (
    .A(not_5_out), .B(multiplexer_44_out), .Cin(fulladder_alu_38_carry), .sum(fulladder_alu_45_sum),
    .carry(fulladder_alu_45_carry));
  Multiplexer multiplexer_45 (
    .in0(multiplexer_44_out), .in1(fulladder_alu_45_sum), .out(multiplexer_45_out), .sel(Q[6]), .en(1'b1));
  fulladder_alu fulladder_alu_46 (
    .A(multiplexer_45_out), .B(not_6_out), .Cin(fulladder_alu_39_carry), .sum(fulladder_alu_46_sum),
    .carry(fulladder_alu_46_carry));
  Multiplexer multiplexer_46 (
    .in0(multiplexer_45_out), .in1(fulladder_alu_46_sum), .out(multiplexer_46_out), .sel(Q[5]), .en(1'b1));
  fulladder_alu fulladder_alu_47 (
    .A(multiplexer_46_out), .B(not_7_out), .Cin(fulladder_alu_40_carry), .sum(fulladder_alu_47_sum),
    .carry(fulladder_alu_47_carry));
  Multiplexer multiplexer_47 (
    .in0(multiplexer_46_out), .in1(fulladder_alu_47_sum), .out(multiplexer_47_out), .sel(Q[4]), .en(1'b1));
  fulladder_alu fulladder_alu_48 (
    .A(multiplexer_47_out), .B(not_8_out), .Cin(fulladder_alu_41_carry), .sum(fulladder_alu_48_sum),
    .carry(fulladder_alu_48_carry));
  Multiplexer multiplexer_48 (
    .in0(multiplexer_47_out), .in1(fulladder_alu_48_sum), .out(multiplexer_48_out), .sel(Q[3]), .en(1'b1));
  fulladder_alu fulladder_alu_49 (
    .A(multiplexer_48_out), .B(not_9_out), .Cin(fulladder_alu_42_carry), .sum(fulladder_alu_49_sum),
    .carry(Q[2]));
  Multiplexer multiplexer_49 (
    .in0(multiplexer_48_out), .in1(fulladder_alu_49_sum), .sel(Q[2]), .en(1'b1));  // open: out
  not not_5 (not_5_out, B_divisor[3]);
  fulladder_alu fulladder_alu_50 (
    .A(not_5_out), .B(not_1_out), .Cin(fulladder_alu_44_carry), .sum(fulladder_alu_50_sum),
    .carry(fulladder_alu_50_carry));
  Multiplexer multiplexer_50 (
    .in0(not_1_out), .in1(fulladder_alu_50_sum), .out(multiplexer_50_out), .sel(Q[7]), .en(1'b1));
  fulladder_alu fulladder_alu_51 (
    .A(not_6_out), .B(multiplexer_50_out), .Cin(fulladder_alu_45_carry), .sum(fulladder_alu_51_sum),
    .carry(fulladder_alu_51_carry));
  Multiplexer multiplexer_51 (
    .in0(multiplexer_50_out), .in1(fulladder_alu_51_sum), .out(multiplexer_51_out), .sel(Q[6]), .en(1'b1));
  fulladder_alu fulladder_alu_52 (
    .A(multiplexer_51_out), .B(not_7_out), .Cin(fulladder_alu_46_carry), .sum(fulladder_alu_52_sum),
    .carry(fulladder_alu_52_carry));
  Multiplexer multiplexer_52 (
    .in0(multiplexer_51_out), .in1(fulladder_alu_52_sum), .out(multiplexer_52_out), .sel(Q[5]), .en(1'b1));
  fulladder_alu fulladder_alu_53 (
    .A(multiplexer_52_out), .B(not_8_out), .Cin(fulladder_alu_47_carry), .sum(fulladder_alu_53_sum),
    .carry(fulladder_alu_53_carry));
  Multiplexer multiplexer_53 (
    .in0(multiplexer_52_out), .in1(fulladder_alu_53_sum), .out(multiplexer_53_out), .sel(Q[4]), .en(1'b1));
  fulladder_alu fulladder_alu_54 (
    .A(multiplexer_53_out), .B(not_9_out), .Cin(fulladder_alu_48_carry), .sum(fulladder_alu_54_sum),
    .carry(Q[3]));
  Multiplexer multiplexer_54 (
    .in0(multiplexer_53_out), .in1(fulladder_alu_54_sum), .sel(Q[3]), .en(1'b1));  // open: out
  not not_6 (not_6_out, B_divisor[4]);
  fulladder_alu fulladder_alu_55 (
    .A(not_6_out), .B(not_1_out), .Cin(fulladder_alu_50_carry), .sum(fulladder_alu_55_sum),
    .carry(fulladder_alu_55_carry));
  Multiplexer multiplexer_55 (
    .in0(not_1_out), .in1(fulladder_alu_55_sum), .out(multiplexer_55_out), .sel(Q[7]), .en(1'b1));
  fulladder_alu fulladder_alu_56 (
    .A(not_7_out), .B(multiplexer_55_out), .Cin(fulladder_alu_51_carry), .sum(fulladder_alu_56_sum),
    .carry(fulladder_alu_56_carry));
  Multiplexer multiplexer_56 (
    .in0(multiplexer_55_out), .in1(fulladder_alu_56_sum), .out(multiplexer_56_out), .sel(Q[6]), .en(1'b1));
  fulladder_alu fulladder_alu_57 (
    .A(multiplexer_56_out), .B(not_8_out), .Cin(fulladder_alu_52_carry), .sum(fulladder_alu_57_sum),
    .carry(fulladder_alu_57_carry));
  Multiplexer multiplexer_57 (
    .in0(multiplexer_56_out), .in1(fulladder_alu_57_sum), .out(multiplexer_57_out), .sel(Q[5]), .en(1'b1));
  fulladder_alu fulladder_alu_58 (
    .A(multiplexer_57_out), .B(not_9_out), .Cin(fulladder_alu_53_carry), .sum(fulladder_alu_58_sum),
    .carry(Q[4]));
  Multiplexer multiplexer_58 (
    .in0(multiplexer_57_out), .in1(fulladder_alu_58_sum), .sel(Q[4]), .en(1'b1));  // open: out
  not not_7 (not_7_out, B_divisor[5]);
  fulladder_alu fulladder_alu_59 (
    .A(not_7_out), .B(not_1_out), .Cin(fulladder_alu_55_carry), .sum(fulladder_alu_59_sum),
    .carry(fulladder_alu_59_carry));
  Multiplexer multiplexer_59 (
    .in0(not_1_out), .in1(fulladder_alu_59_sum), .out(multiplexer_59_out), .sel(Q[7]), .en(1'b1));
  fulladder_alu fulladder_alu_60 (
    .A(not_8_out), .B(multiplexer_59_out), .Cin(fulladder_alu_56_carry), .sum(fulladder_alu_60_sum),
    .carry(fulladder_alu_60_carry));
  Multiplexer multiplexer_60 (
    .in0(multiplexer_59_out), .in1(fulladder_alu_60_sum), .out(multiplexer_60_out), .sel(Q[6]), .en(1'b1));
  fulladder_alu fulladder_alu_61 (
    .A(multiplexer_60_out), .B(not_9_out), .Cin(fulladder_alu_57_carry), .sum(fulladder_alu_61_sum),
    .carry(Q[5]));
  Multiplexer multiplexer_61 (
    .in0(multiplexer_60_out), .in1(fulladder_alu_61_sum), .sel(Q[5]), .en(1'b1));  // open: out
  not not_8 (not_8_out, B_divisor[6]);
  fulladder_alu fulladder_alu_62 (
    .A(not_8_out), .B(not_1_out), .Cin(fulladder_alu_59_carry), .sum(fulladder_alu_62_sum),
    .carry(fulladder_alu_62_carry));
  Multiplexer multiplexer_62 (
    .in0(not_1_out), .in1(fulladder_alu_62_sum), .out(multiplexer_62_out), .sel(Q[7]), .en(1'b1));
  fulladder_alu fulladder_alu_63 (
    .A(not_9_out), .B(multiplexer_62_out), .Cin(fulladder_alu_60_carry), .sum(fulladder_alu_63_sum),
    .carry(Q[6]));
  Multiplexer multiplexer_63 (
    .in0(multiplexer_62_out), .in1(fulladder_alu_63_sum), .sel(Q[6]), .en(1'b1));  // open: out
  not not_9 (not_9_out, B_divisor[7]);
  fulladder_alu fulladder_alu_64 (
    .A(not_9_out), .B(not_1_out), .Cin(fulladder_alu_62_carry), .sum(fulladder_alu_64_sum), .carry(Q[7]));
  Multiplexer multiplexer_64 (.in0(not_1_out), .in1(fulladder_alu_64_sum), .sel(Q[7]), .en(1'b1));  // open: out

  assign Q[15:8] = {8{1'b0}};
  assign Remainder[15:8] = {8{1'b0}};

  // Notes on the sheet:
  //                B(Divisor)
  //   A(dividend)
  //   Quotient 
endmodule

module hexa (
  input  in_1,
  output a,
  output b,
  output c,
  output d,
  output e,
  output f,
  output g
);

  wire clock_1_out, j_k_ff_1_q, j_k_ff_2_q, j_k_ff_3_q, j_k_ff_4_q, nand_1_out, nand_2_out, nand_3_out,
       nand_4_out, nand_5_out, nand_6_out, nand_7_out, nand_8_out, nand_9_out, nand_10_out, nand_11_out,
       nand_12_out, nand_13_out, nand_14_out, nand_15_out, nand_16_out, nand_17_out, nand_18_out,
       nand_19_out, nand_20_out, nand_21_out, nand_22_out, nand_23_out, nand_24_out, nand_25_out,
       nand_26_out, nand_27_out, nand_28_out, nand_29_out, nand_30_out, nand_31_out, nand_32_out,
       nand_33_out, nand_34_out, nand_35_out, nand_36_out, nand_37_out, nand_38_out, nand_39_out,
       nand_40_out, nand_41_out, nand_42_out, nand_43_out, nand_44_out, nand_45_out, nand_46_out,
       nand_47_out, nand_48_out, nand_49_out, nand_50_out, nand_51_out, nand_52_out, nand_53_out,
       nand_54_out, nand_55_out, nand_56_out, nand_57_out, nand_58_out, nand_59_out, nand_60_out,
       nand_61_out, nand_62_out, nand_63_out, nand_64_out, nand_65_out, nand_66_out, nand_67_out,
       nand_68_out, nand_69_out, nand_70_out, nand_71_out, nand_72_out, nand_73_out, nand_74_out,
       nand_75_out, nand_76_out, nand_77_out, nand_78_out, nand_79_out, nand_80_out, nand_81_out,
       nand_82_out, nand_83_out, nand_84_out, nand_85_out, nand_86_out, nand_87_out, nand_88_out,
       nand_89_out, nand_90_out, nand_91_out, nand_92_out, nand_93_out, nand_94_out, nand_95_out,
       nand_96_out, nand_97_out, nand_98_out, nand_99_out, nand_100_out, nand_101_out, nand_102_out,
       nand_103_out, nand_104_out, nand_105_out, nand_107_out, nand_108_out, nand_109_out, nand_110_out,
       nand_111_out, nand_112_out, nand_113_out, nand_114_out, nand_115_out, nand_116_out, nand_117_out,
       nand_118_out, nand_119_out, nand_120_out, nand_121_out, nand_122_out, nand_123_out, nand_124_out,
       nand_125_out, nand_126_out, nand_127_out, nand_128_out, nand_129_out, nand_130_out, nand_131_out,
       nand_132_out, nand_133_out, nand_134_out, nand_135_out, nand_137_out, nand_138_out, nand_139_out,
       nand_140_out, nand_142_out, nand_143_out, nand_144_out, nand_145_out, nand_146_out, nand_147_out,
       nand_148_out, nand_149_out, not_1_out, not_2_out, not_3_out, not_4_out;

  Clock clock_1 (.out(clock_1_out));
  LED led_1 (.in(not_1_out));
  not not_1 (not_1_out, j_k_ff_1_q);
  J_K_Flip_Flop j_k_ff_1 (
    .J(in_1), .clk(clock_1_out), .K(in_1), .Q(j_k_ff_1_q), .en(nand_1_out));  // open: Qn, preset, reset
  J_K_Flip_Flop j_k_ff_2 (
    .J(in_1), .clk(j_k_ff_1_q), .K(in_1), .Q(j_k_ff_2_q), .en(nand_1_out));  // open: Qn, preset, reset
  LED led_2 (.in(not_2_out));
  not not_2 (not_2_out, j_k_ff_2_q);
  J_K_Flip_Flop j_k_ff_3 (
    .J(in_1), .clk(j_k_ff_2_q), .K(in_1), .Q(j_k_ff_3_q), .en(nand_1_out));  // open: Qn, preset, reset
  LED led_3 (.in(not_3_out));
  not not_3 (not_3_out, j_k_ff_3_q);
  J_K_Flip_Flop j_k_ff_4 (
    .J(in_1), .clk(j_k_ff_3_q), .K(in_1), .Q(j_k_ff_4_q), .en(nand_1_out));  // open: Qn, preset, reset
  LED led_4 (.in(not_4_out));
  not not_4 (not_4_out, j_k_ff_4_q);
  nand nand_1 (nand_1_out, j_k_ff_1_q, j_k_ff_2_q, j_k_ff_3_q, clock_1_out);
  nand nand_2 (nand_2_out, not_3_out, not_3_out);
  nand nand_3 (nand_3_out, not_4_out, not_4_out);
  nand nand_4 (nand_4_out, not_2_out, not_2_out);
  nand nand_5 (nand_5_out, not_4_out, not_4_out);
  nand nand_6 (nand_6_out, not_2_out, not_2_out);
  nand nand_7 (nand_7_out, not_4_out, not_4_out);
  nand nand_8 (nand_8_out, not_4_out, not_4_out);
  nand nand_9 (nand_9_out, not_3_out, not_3_out);
  nand nand_10 (nand_10_out, not_3_out, not_3_out);
  nand nand_11 (nand_11_out, not_3_out, not_3_out);
  nand nand_12 (nand_12_out, not_1_out, not_1_out);
  nand nand_13 (nand_13_out, not_1_out, not_1_out);
  nand nand_14 (nand_14_out, not_4_out, not_4_out);
  nand nand_15 (nand_15_out, not_3_out, not_3_out);
  nand nand_16 (nand_16_out, not_1_out, not_1_out);
  nand nand_17 (nand_17_out, not_4_out, not_4_out);
  nand nand_18 (nand_18_out, not_4_out, nand_2_out);
  nand nand_19 (nand_19_out, nand_3_out, nand_4_out);
  nand nand_20 (nand_20_out, nand_5_out, nand_6_out);
  nand nand_21 (nand_21_out, nand_7_out, not_1_out);
  nand nand_22 (nand_22_out, nand_8_out, nand_9_out);
  nand nand_23 (nand_23_out, nand_10_out, not_2_out);
  nand nand_24 (nand_24_out, nand_11_out, nand_12_out);
  nand nand_25 (nand_25_out, not_2_out, nand_13_out);
  nand nand_26 (nand_26_out, not_4_out, not_2_out);
  nand nand_27 (nand_27_out, not_4_out, not_3_out);
  nand nand_28 (nand_28_out, nand_14_out, not_3_out);
  nand nand_29 (nand_29_out, nand_15_out, not_2_out);
  nand nand_30 (nand_30_out, not_2_out, nand_16_out);
  nand nand_31 (nand_31_out, nand_17_out, not_3_out);
  nand nand_32 (nand_32_out, not_3_out, not_3_out);
  nand nand_33 (nand_33_out, not_1_out, not_1_out);
  nand nand_34 (nand_34_out, not_4_out, not_4_out);
  nand nand_35 (nand_35_out, not_4_out, not_4_out);
  nand nand_36 (nand_36_out, nand_18_out, nand_18_out);
  nand nand_37 (nand_37_out, not_2_out, not_2_out);
  nand nand_38 (nand_38_out, not_4_out, not_4_out);
  nand nand_39 (nand_39_out, not_3_out, not_3_out);
  nand nand_40 (nand_40_out, nand_19_out, nand_19_out);
  nand nand_41 (nand_41_out, not_1_out, not_1_out);
  nand nand_42 (nand_42_out, not_4_out, not_4_out);
  nand nand_43 (nand_43_out, not_2_out, not_2_out);
  nand nand_44 (nand_44_out, nand_20_out, nand_21_out);
  nand nand_45 (nand_45_out, not_2_out, not_2_out);
  nand nand_46 (nand_46_out, not_4_out, not_4_out);
  nand nand_47 (nand_47_out, not_3_out, not_3_out);
  nand nand_48 (nand_48_out, nand_22_out, nand_22_out);
  nand nand_49 (nand_49_out, not_1_out, not_1_out);
  nand nand_50 (nand_50_out, nand_23_out, nand_23_out);
  nand nand_51 (nand_51_out, not_2_out, not_2_out);
  nand nand_52 (nand_52_out, not_2_out, not_2_out);
  nand nand_53 (nand_53_out, nand_24_out, nand_25_out);
  nand nand_54 (nand_54_out, nand_26_out, nand_27_out);
  nand nand_55 (nand_55_out, not_2_out, not_2_out);
  nand nand_56 (nand_56_out, not_1_out, not_1_out);
  nand nand_57 (nand_57_out, nand_28_out, nand_28_out);
  nand nand_58 (nand_58_out, not_2_out, not_2_out);
  nand nand_59 (nand_59_out, nand_29_out, nand_30_out);
  nand nand_60 (nand_60_out, nand_31_out, nand_31_out);
  nand nand_61 (nand_61_out, not_2_out, not_2_out);
  nand nand_62 (nand_62_out, not_3_out, not_3_out);
  nand nand_63 (nand_63_out, nand_32_out, nand_33_out);
  nand nand_64 (nand_64_out, nand_34_out, not_2_out);
  nand nand_65 (nand_65_out, nand_35_out, not_3_out);
  nand nand_66 (nand_66_out, not_3_out, not_2_out);
  nand nand_67 (nand_67_out, nand_36_out, nand_37_out);
  nand nand_68 (nand_68_out, nand_38_out, nand_39_out);
  nand nand_69 (nand_69_out, nand_40_out, nand_41_out);
  nand nand_70 (nand_70_out, nand_42_out, not_2_out);
  nand nand_71 (nand_71_out, not_4_out, nand_43_out);
  nand nand_72 (nand_72_out, nand_44_out, nand_44_out);
  nand nand_73 (nand_73_out, nand_45_out, not_1_out);
  nand nand_74 (nand_74_out, nand_46_out, not_3_out);
  nand nand_75 (nand_75_out, not_4_out, nand_47_out);
  nand nand_76 (nand_76_out, nand_48_out, nand_49_out);
  nand nand_77 (nand_77_out, nand_50_out, not_1_out);
  nand nand_78 (nand_78_out, not_3_out, nand_51_out);
  nand nand_79 (nand_79_out, not_3_out, not_2_out);
  nand nand_80 (nand_80_out, not_4_out, nand_52_out);
  nand nand_81 (nand_81_out, nand_53_out, nand_53_out);
  nand nand_82 (nand_82_out, nand_54_out, nand_54_out);
  nand nand_83 (nand_83_out, nand_55_out, nand_56_out);
  nand nand_84 (nand_84_out, nand_57_out, nand_58_out);
  nand nand_85 (nand_85_out, nand_59_out, nand_59_out);
  nand nand_86 (nand_86_out, nand_60_out, nand_61_out);
  nand nand_87 (nand_87_out, not_4_out, nand_62_out);
  nand nand_88 (nand_88_out, not_4_out, not_1_out);
  nand nand_89 (nand_89_out, nand_63_out, nand_64_out);
  nand nand_90 (nand_90_out, nand_65_out, nand_65_out);
  nand nand_91 (nand_91_out, nand_66_out, nand_67_out);
  nand nand_92 (nand_92_out, not_1_out, not_1_out);
  nand nand_93 (nand_93_out, nand_68_out, nand_69_out);
  nand nand_94 (nand_94_out, not_3_out, not_3_out);
  nand nand_95 (nand_95_out, not_1_out, not_1_out);
  nand nand_96 (nand_96_out, nand_70_out, nand_70_out);
  nand nand_97 (nand_97_out, nand_71_out, nand_71_out);
  nand nand_98 (nand_98_out, nand_72_out, nand_73_out);
  nand nand_99 (nand_99_out, nand_74_out, nand_75_out);
  nand nand_100 (nand_100_out, nand_76_out, nand_77_out);
  nand nand_101 (nand_101_out, nand_78_out, nand_78_out);
  nand nand_102 (nand_102_out, nand_79_out, nand_79_out);
  nand nand_103 (nand_103_out, not_1_out, not_1_out);
  nand nand_104 (nand_104_out, nand_80_out, nand_80_out);
  nand nand_105 (nand_105_out, not_1_out, not_1_out);
  nand nand_106 (e, nand_81_out, nand_82_out);
  nand nand_107 (nand_107_out, nand_83_out, nand_84_out);
  nand nand_108 (nand_108_out, not_1_out, not_1_out);
  nand nand_109 (nand_109_out, not_3_out, not_3_out);
  nand nand_110 (nand_110_out, nand_85_out, nand_86_out);
  nand nand_111 (nand_111_out, nand_87_out, nand_88_out);
  nand nand_112 (nand_112_out, nand_89_out, nand_89_out);
  nand nand_113 (nand_113_out, nand_90_out, not_1_out);
  nand nand_114 (nand_114_out, nand_91_out, nand_91_out);
  nand nand_115 (nand_115_out, not_4_out, nand_92_out);
  nand nand_116 (nand_116_out, nand_93_out, nand_93_out);
  nand nand_117 (nand_117_out, nand_94_out, nand_95_out);
  nand nand_118 (nand_118_out, nand_96_out, not_1_out);
  nand nand_119 (nand_119_out, nand_97_out, not_1_out);
  nand nand_120 (nand_120_out, nand_98_out, nand_98_out);
  nand nand_121 (nand_121_out, nand_99_out, nand_99_out);
  nand nand_122 (nand_122_out, nand_100_out, nand_100_out);
  nand nand_123 (nand_123_out, nand_101_out, not_1_out);
  nand nand_124 (nand_124_out, nand_102_out, nand_103_out);
  nand nand_125 (nand_125_out, nand_104_out, nand_105_out);
  nand nand_126 (nand_126_out, nand_107_out, nand_107_out);
  nand nand_127 (nand_127_out, not_3_out, nand_108_out);
  nand nand_128 (nand_128_out, not_4_out, nand_109_out);
  nand nand_129 (nand_129_out, not_4_out, not_2_out);
  nand nand_130 (nand_130_out, nand_110_out, nand_110_out);
  nand nand_131 (nand_131_out, nand_111_out, nand_111_out);
  nand nand_132 (nand_132_out, nand_112_out, nand_113_out);
  nand nand_133 (nand_133_out, nand_114_out, nand_115_out);
  nand nand_134 (nand_134_out, nand_116_out, nand_117_out);
  nand nand_135 (nand_135_out, nand_118_out, nand_119_out);
  nand nand_136 (c, nand_120_out, nand_121_out);
  nand nand_137 (nand_137_out, nand_122_out, nand_123_out);
  nand nand_138 (nand_138_out, nand_124_out, nand_125_out);
  nand nand_139 (nand_139_out, nand_126_out, nand_127_out);
  nand nand_140 (nand_140_out, nand_128_out, nand_129_out);
  nand nand_141 (g, nand_130_out, nand_131_out);
  nand nand_142 (nand_142_out, nand_132_out, nand_132_out);
  nand nand_143 (nand_143_out, nand_133_out, nand_133_out);
  nand nand_144 (nand_144_out, nand_134_out, nand_134_out);
  nand nand_145 (nand_145_out, nand_135_out, nand_135_out);
  nand nand_146 (nand_146_out, nand_137_out, nand_137_out);
  nand nand_147 (nand_147_out, nand_138_out, nand_138_out);
  nand nand_148 (nand_148_out, nand_139_out, nand_139_out);
  nand nand_149 (nand_149_out, nand_140_out, nand_140_out);
  nand nand_150 (a, nand_142_out, nand_143_out);
  nand nand_151 (b, nand_144_out, nand_145_out);
  nand nand_152 (d, nand_146_out, nand_147_out);
  nand nand_153 (f, nand_148_out, nand_149_out);
  _7_Segment_Display u_7_segment_display_1 (.g(g), .f(f), .a(a), .b(b), .e(e), .d(d), .c(c));  // open: dp
endmodule

module addition (
  input  [7:0] in_1,
  input  [7:0] in_2,
  output [15:0] out_3
);

  wire fulladder_alu_1_carry, fulladder_alu_2_carry, fulladder_alu_3_carry, fulladder_alu_4_carry,
       fulladder_alu_5_carry, fulladder_alu_6_carry, fulladder_alu_7_carry;

  fulladder_alu fulladder_alu_1 (.A(1'b0), .B(in_1[0]), .Cin(in_2[0]), .sum(out_3[0]), .carry(fulladder_alu_1_carry));
  fulladder_alu fulladder_alu_2 (
    .A(fulladder_alu_1_carry), .B(in_1[1]), .Cin(in_2[1]), .sum(out_3[1]), .carry(fulladder_alu_2_carry));
  fulladder_alu fulladder_alu_3 (
    .A(fulladder_alu_2_carry), .B(in_1[2]), .Cin(in_2[2]), .sum(out_3[2]), .carry(fulladder_alu_3_carry));
  fulladder_alu fulladder_alu_4 (
    .A(fulladder_alu_3_carry), .B(in_1[3]), .Cin(in_2[3]), .sum(out_3[3]), .carry(fulladder_alu_4_carry));
  fulladder_alu fulladder_alu_5 (
    .A(fulladder_alu_4_carry), .B(in_1[4]), .Cin(in_2[4]), .sum(out_3[4]), .carry(fulladder_alu_5_carry));
  fulladder_alu fulladder_alu_6 (
    .A(fulladder_alu_5_carry), .B(in_1[5]), .Cin(in_2[5]), .sum(out_3[5]), .carry(fulladder_alu_6_carry));
  fulladder_alu fulladder_alu_7 (
    .A(fulladder_alu_6_carry), .B(in_1[6]), .Cin(in_2[6]), .sum(out_3[6]), .carry(fulladder_alu_7_carry));
  fulladder_alu fulladder_alu_8 (
    .A(fulladder_alu_7_carry), .B(in_1[7]), .Cin(in_2[7]), .sum(out_3[7]), .carry(out_3[8]));

  assign out_3[15:9] = {7{1'b0}};

  // Notes on the sheet:
  //   A
  //   B
  //   C1
  //   C2
  //   C3
  //   C4
  //   C5
  //   C6
  //   C7
  //   MSB
endmodule

module subtractor (
  input  [7:0] in_1,
  input  [7:0] in_2,
  output [8:0] out_3
);

  wire fulladder_alu_1_carry, fulladder_alu_2_carry, fulladder_alu_3_carry, fulladder_alu_4_carry,
       fulladder_alu_5_carry, fulladder_alu_6_carry, fulladder_alu_7_carry, xor_1_out, xor_2_out, xor_3_out,
       xor_4_out, xor_5_out, xor_6_out, xor_7_out, xor_8_out;

  xor xor_1 (xor_1_out, 1'b1, in_2[0]);
  xor xor_2 (xor_2_out, 1'b1, in_2[1]);
  xor xor_3 (xor_3_out, 1'b1, in_2[2]);
  xor xor_4 (xor_4_out, 1'b1, in_2[3]);
  xor xor_5 (xor_5_out, 1'b1, in_2[4]);
  xor xor_6 (xor_6_out, 1'b1, in_2[5]);
  xor xor_7 (xor_7_out, 1'b1, in_2[6]);
  xor xor_8 (xor_8_out, 1'b1, in_2[7]);
  fulladder_alu fulladder_alu_1 (.A(1'b1), .B(in_1[0]), .Cin(xor_1_out), .sum(out_3[0]), .carry(fulladder_alu_1_carry));
  fulladder_alu fulladder_alu_2 (
    .A(fulladder_alu_1_carry), .B(in_1[1]), .Cin(xor_2_out), .sum(out_3[1]), .carry(fulladder_alu_2_carry));
  fulladder_alu fulladder_alu_3 (
    .A(fulladder_alu_2_carry), .B(in_1[2]), .Cin(xor_3_out), .sum(out_3[2]), .carry(fulladder_alu_3_carry));
  fulladder_alu fulladder_alu_4 (
    .A(fulladder_alu_3_carry), .B(in_1[3]), .Cin(xor_4_out), .sum(out_3[3]), .carry(fulladder_alu_4_carry));
  fulladder_alu fulladder_alu_5 (
    .A(fulladder_alu_4_carry), .B(in_1[4]), .Cin(xor_5_out), .sum(out_3[4]), .carry(fulladder_alu_5_carry));
  fulladder_alu fulladder_alu_6 (
    .A(fulladder_alu_5_carry), .B(in_1[5]), .Cin(xor_6_out), .sum(out_3[5]), .carry(fulladder_alu_6_carry));
  fulladder_alu fulladder_alu_7 (
    .A(fulladder_alu_6_carry), .B(in_1[6]), .Cin(xor_7_out), .sum(out_3[6]), .carry(fulladder_alu_7_carry));
  fulladder_alu fulladder_alu_8 (
    .A(fulladder_alu_7_carry), .B(in_1[7]), .Cin(xor_8_out), .sum(out_3[7]), .carry(out_3[8]));

  // Notes on the sheet:
  //   A
  //   B
  //   difference
endmodule

module converter (
  input  MSB,
  input  in_2,
  input  in_3,
  input  LSB,
  output out_5,
  output out_6,
  output out_7,
  output out_8,
  output out_9,
  output out_10,
  output out_11
);

  wire and_1_out, and_2_out, and_3_out, and_4_out, and_5_out, and_6_out, and_7_out, and_8_out, and_9_out,
       and_10_out, and_11_out, and_12_out, and_13_out, and_14_out, and_15_out, and_16_out, and_17_out,
       and_18_out, and_19_out, and_20_out, and_21_out, and_22_out, and_23_out, and_24_out, and_25_out,
       and_26_out, and_27_out, and_28_out, and_29_out, and_30_out, and_31_out, and_32_out, and_33_out,
       and_34_out, and_35_out, and_36_out, and_37_out, not_1_out, not_2_out, not_3_out, not_4_out, not_5_out,
       not_6_out, not_7_out, not_8_out, not_9_out, not_10_out, not_11_out, not_12_out, not_13_out,
       not_14_out, not_15_out, not_16_out, not_17_out, not_18_out, not_19_out, not_20_out, not_21_out,
       not_22_out, not_23_out, not_24_out, not_25_out, not_26_out, not_27_out, not_28_out, not_29_out,
       not_30_out, not_31_out, not_32_out, not_33_out, not_34_out, not_35_out, not_36_out, not_37_out,
       not_38_out, not_39_out, not_40_out, not_41_out, not_42_out, not_43_out, not_44_out, not_45_out,
       not_46_out, not_47_out, not_48_out, not_49_out, not_50_out;

  not not_1 (not_1_out, MSB);
  not not_2 (not_2_out, in_2);
  not not_3 (not_3_out, MSB);
  not not_4 (not_4_out, in_3);
  not not_5 (not_5_out, LSB);
  not not_6 (not_6_out, in_2);
  not not_7 (not_7_out, in_3);
  not not_8 (not_8_out, in_2);
  not not_9 (not_9_out, LSB);
  not not_10 (not_10_out, MSB);
  not not_11 (not_11_out, in_3);
  not not_12 (not_12_out, MSB);
  not not_13 (not_13_out, in_3);
  not not_14 (not_14_out, MSB);
  not not_15 (not_15_out, in_3);
  not not_16 (not_16_out, MSB);
  not not_17 (not_17_out, in_2);
  not not_18 (not_18_out, MSB);
  not not_19 (not_19_out, in_2);
  not not_20 (not_20_out, LSB);
  not not_21 (not_21_out, in_2);
  not not_22 (not_22_out, in_3);
  not not_23 (not_23_out, LSB);
  not not_24 (not_24_out, in_3);
  not not_25 (not_25_out, MSB);
  not not_26 (not_26_out, in_2);
  not not_27 (not_27_out, LSB);
  not not_28 (not_28_out, in_2);
  not not_29 (not_29_out, in_3);
  not not_30 (not_30_out, LSB);
  not not_31 (not_31_out, MSB);
  not not_32 (not_32_out, LSB);
  not not_33 (not_33_out, in_3);
  not not_34 (not_34_out, LSB);
  not not_35 (not_35_out, MSB);
  not not_36 (not_36_out, in_3);
  not not_37 (not_37_out, LSB);
  not not_38 (not_38_out, in_2);
  not not_39 (not_39_out, in_2);
  not not_40 (not_40_out, LSB);
  not not_41 (not_41_out, MSB);
  not not_42 (not_42_out, MSB);
  not not_43 (not_43_out, in_2);
  not not_44 (not_44_out, in_3);
  not not_45 (not_45_out, LSB);
  not not_46 (not_46_out, in_2);
  not not_47 (not_47_out, LSB);
  not not_48 (not_48_out, MSB);
  not not_49 (not_49_out, in_3);
  not not_50 (not_50_out, in_2);
  and and_1 (and_1_out, not_1_out, not_2_out);
  and and_2 (and_2_out, not_3_out, not_4_out, not_5_out);
  and and_3 (and_3_out, not_6_out, not_7_out);
  and and_4 (and_4_out, not_8_out, not_9_out);
  and and_5 (and_5_out, not_10_out, in_3, LSB);
  and and_6 (and_6_out, MSB, not_11_out, LSB);
  and and_7 (and_7_out, not_12_out, not_13_out);
  and and_8 (and_8_out, not_14_out, LSB);
  and and_9 (and_9_out, not_15_out, LSB);
  and and_10 (and_10_out, not_16_out, in_2);
  and and_11 (and_11_out, MSB, not_17_out);
  and and_12 (and_12_out, not_18_out, not_19_out, not_20_out);
  and and_13 (and_13_out, not_21_out, in_3, LSB);
  and and_14 (and_14_out, in_2, not_22_out, LSB);
  and and_15 (and_15_out, in_2, in_3, not_23_out);
  and and_16 (and_16_out, MSB, not_24_out);
  and and_17 (and_17_out, not_25_out, not_26_out, not_27_out);
  and and_18 (and_18_out, not_28_out, not_29_out, not_30_out);
  and and_19 (and_19_out, not_31_out, in_3, not_32_out);
  and and_20 (and_20_out, MSB, in_3, LSB);
  and and_21 (and_21_out, MSB, in_2);
  and and_22 (and_22_out, not_33_out, not_34_out);
  and and_23 (and_23_out, not_35_out, in_2, not_36_out);
  and and_24 (and_24_out, in_2, not_37_out);
  and and_25 (and_25_out, MSB, not_38_out);
  and and_26 (and_26_out, MSB, in_3);
  and and_27 (and_27_out, not_39_out, not_40_out);
  and and_28 (and_28_out, not_41_out, in_3);
  and and_29 (and_29_out, not_42_out, in_2, LSB);
  and and_30 (and_30_out, in_2, in_3);
  and and_31 (and_31_out, MSB, not_43_out, not_44_out);
  and and_32 (and_32_out, MSB, not_45_out);
  and and_33 (and_33_out, not_46_out, in_3);
  and and_34 (and_34_out, in_3, not_47_out);
  and and_35 (and_35_out, not_48_out, in_2, not_49_out);
  and and_36 (and_36_out, MSB, not_50_out);
  and and_37 (and_37_out, MSB, LSB);
  or or_1 (out_5, and_1_out, and_2_out, and_3_out, and_4_out, and_5_out, and_6_out);
  or or_2 (out_6, and_7_out, and_8_out, and_9_out, and_10_out, and_11_out);
  or or_3 (out_7, and_12_out, and_13_out, and_14_out, and_15_out, and_16_out);
  or or_4 (out_8, and_17_out, and_18_out, and_19_out, and_20_out, and_21_out);
  or or_5 (out_9, and_22_out, and_23_out, and_24_out, and_25_out, and_26_out);
  or or_6 (out_10, and_27_out, and_28_out, and_29_out, and_30_out, and_31_out, and_32_out);
  or or_7 (out_11, and_33_out, and_34_out, and_35_out, and_36_out, and_37_out);
endmodule
